// Logisim project 3lab.circ as structural Verilog: 4 circuits, main circuit main
module main (
  input  R,
  input  S,
  output Q,
  output notQ
);

  nor nor_1 (Q, R, notQ);
  nor nor_2 (notQ, Q, S);
endmodule

module srLatch (
  input  R,
  input  S,
  output Q,
  output notQ
);

  nor nor_1 (Q, R, notQ);
  nor nor_2 (notQ, Q, S);
endmodule

module dLatch (
  input  CLK,
  input  D,
  output Q,
  output notQ
);

  wire and_1_out, and_2_out, not_1_out;

  not not_1 (not_1_out, D);
  and and_1 (and_1_out, CLK, not_1_out);
  and and_2 (and_2_out, CLK, D);
  srLatch srlatch_1 (.R(and_1_out), .S(and_2_out), .Q(Q), .notQ(notQ));
endmodule

module dflipflops (
  input  in_1,
  input  D,
  output Q
);

  wire dlatch_1_q;

  dLatch dlatch_1 (.CLK(in_1), .D(D), .Q(dlatch_1_q));  // open: notQ
  dLatch dlatch_2 (.CLK(in_1), .D(dlatch_1_q), .Q(Q));  // open: notQ
endmodule
